# Fritzing sketch pi-badge layout (saved by Fritzing 0.9.2b)

parts:
  Part1 = Arduino Yun
  Part2 = Color Sensor Breakout ADJD-S311

nets:
  N1: Part1.ICSP_SCK, Part2.SCK
  N2: Part1.ICSP_MOSI, Part2.SDA
  N3: Part1.D2, Part2.CS
  N4: Part1.D3_PWM, Part2.RESET
  N5: Part1.D4, Part2.A0
  N6: Part1.3V3, Part2.LED
  5V: Part1.5V, Part2.VCC
  GND: Part1.GND, Part2.GND

custom parts:
  Color Sensor Breakout ADJD-S311: Description: The ADJD-S311-CR999 is a great little color light sensor. In fact, it's so little that it can be pretty difficult to play with, so we made this evaluation board! It provides all the necessary support circuitry to discern the smallest differences between visible colors. Dimensions: 21.6x12.7mm (0.85x0.50") Documents: Schematic Eagle Files Datasheet (ADJD-S311) Example Arduino Code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
